// Logisim project F6.circ as structural Verilog: 8 circuits, main circuit main
module main (
  input  in_1,
  input  in_2,
  output [31:0] out_3,
  output [31:0] out_4
);

  wire clock_1_out, Decoding_decode_is_addi, Decoding_decode_is_imm;
  wire [2:0] Decoding_decode_funct3;
  wire [4:0] Decoding_decode_rd, Decoding_decode_rs1;
  wire [6:0] Decoding_decode_opcode;
  wire [9:0] module_splitter_1_splitter_output;
  wire [11:0] Decoding_decode_imm_raw;
  wire [31:0] module_adder_1_adder_output, rom_1_data;

  Clock clock_1 (.out(clock_1_out));
  Module_PC module_pc_1 (
    .Pc_input(module_adder_1_adder_output), .Pc_We(in_1), .Pc_Clk(clock_1_out), .Pc_R(in_2), .Pc_Output(out_3));
  Module_adder module_adder_1 (.Adder_Input(out_3), .Adder_Output(module_adder_1_adder_output));
  Module_Splitter module_splitter_1 (.Splitter_input(out_3), .Splitter_Output(module_splitter_1_splitter_output));
  ROM #(.addrWidth(10), .dataWidth(32)) rom_1 (.addr(module_splitter_1_splitter_output), .data(rom_1_data));
  Module_Decode Decoding (
    .Decoder_Input(rom_1_data), .Decode_Is_Addi(Decoding_decode_is_addi),
    .Decode_Opcode(Decoding_decode_opcode), .Decode_Rd(Decoding_decode_rd),
    .Decode_is_imm(Decoding_decode_is_imm), .Decode_Funct3(Decoding_decode_funct3),
    .Decode_Rs1(Decoding_decode_rs1), .Decode_imm_raw(Decoding_decode_imm_raw));
  Bit_Extender Sign_Extention (.Bit_Extender_Input(Decoding_decode_imm_raw), .Bit_Extender_Output(out_4));
  Register_File register_file_1 (
    .Register_File_Is_Addi(Decoding_decode_is_addi), .Register_File_Is_Jalr(Decoding_decode_is_imm),
    .Register_File_Select(Decoding_decode_rd), .Reset(in_2), .Register_File_Clk(clock_1_out));

  // Notes on the sheet:
  //   contents of rom_1 (hex, n*v repeats v):
  //   1400513 10000e7 fff00293
endmodule

module Module_adder (
  input  [31:0] Adder_Input,
  output [31:0] Adder_Output
);

  Adder #(.width(32)) adder_1 (.a(32'h4), .b(Adder_Input), .out(Adder_Output));  // open: cin, cout
endmodule

module Module_PC (
  input  [31:0] Pc_input,
  input  Pc_We,
  input  Pc_Clk,
  input  Pc_R,
  output [31:0] Pc_Output
);

  Register #(.width(32)) Pc (.D(Pc_input), .en(Pc_We), .clk(Pc_Clk), .Q(Pc_Output), .clr(Pc_R));
endmodule

module Module_Splitter (
  input  [31:0] Splitter_input,
  output [9:0] Splitter_Output
);


  assign Splitter_Output = Splitter_input[11:2];
endmodule

module Module_Rom (
  input  [9:0] Rom_Input,
  output [31:0] Rom_Output
);

  ROM #(.addrWidth(10), .dataWidth(32)) rom_1 (.addr(Rom_Input), .data(Rom_Output));
endmodule

module Module_Decode (
  input  [31:0] Decoder_Input,
  output Decode_Is_Addi,
  output [6:0] Decode_Opcode,
  output [4:0] Decode_Rd,
  output Decode_is_imm,
  output [2:0] Decode_Funct3,
  output [4:0] Decode_Rs1,
  output [11:0] Decode_imm_raw
);

  Comparator #(.width(7)) comparator_1 (.a(Decoder_Input[6:0]), .b(7'b0010011), .eq(Decode_Is_Addi));  // open: gt, lt
  Comparator #(.width(7)) comparator_2 (.a(Decoder_Input[6:0]), .b(7'b1100111), .eq(Decode_is_imm));  // open: gt, lt

  assign Decode_Funct3 = Decoder_Input[14:12];
  assign Decode_imm_raw = Decoder_Input[31:20];
  assign Decode_Opcode = Decoder_Input[6:0];
  assign Decode_Rd = Decoder_Input[11:7];
  assign Decode_Rs1 = Decoder_Input[19:15];
endmodule

module Bit_Extender (
  input  [11:0] Bit_Extender_Input,
  output [31:0] Bit_Extender_Output
);

  assign Bit_Extender_Output = {{20{Bit_Extender_Input[11]}}, Bit_Extender_Input};  // Bit_Extender_part bit_extender_1
endmodule

module Register_File (
  input  Register_File_Is_Addi,
  input  Register_File_Is_Jalr,
  input  [4:0] Register_File_Select,
  input  Reset,
  input  Register_File_Clk
);

  wire decoder_1_out1, decoder_1_out2, decoder_1_out3, decoder_1_out4, decoder_1_out5, decoder_1_out6,
       decoder_1_out7, decoder_1_out8, decoder_1_out9, decoder_1_out10, decoder_1_out11, decoder_1_out12,
       decoder_1_out13, decoder_1_out14, decoder_1_out15, decoder_1_out16, decoder_1_out17, decoder_1_out18,
       decoder_1_out19, decoder_1_out20, decoder_1_out21, decoder_1_out22, decoder_1_out23, decoder_1_out24,
       decoder_1_out25, decoder_1_out26, decoder_1_out27, decoder_1_out28, decoder_1_out29, decoder_1_out30,
       decoder_1_out31, or_1_out;
  wire [4:0] undriven;
  wire [31:0] x0_q;

  or or_1 (or_1_out, Register_File_Is_Addi, Register_File_Is_Jalr);
  Decoder #(.select(5)) decoder_1 (
    .out1(decoder_1_out1), .out2(decoder_1_out2), .out3(decoder_1_out3), .out4(decoder_1_out4),
    .out5(decoder_1_out5), .out6(decoder_1_out6), .out7(decoder_1_out7), .out8(decoder_1_out8),
    .out9(decoder_1_out9), .out10(decoder_1_out10), .out11(decoder_1_out11), .out12(decoder_1_out12),
    .out13(decoder_1_out13), .out14(decoder_1_out14), .out15(decoder_1_out15), .out16(decoder_1_out16),
    .out17(decoder_1_out17), .out18(decoder_1_out18), .out19(decoder_1_out19), .out20(decoder_1_out20),
    .out21(decoder_1_out21), .out22(decoder_1_out22), .out23(decoder_1_out23), .out24(decoder_1_out24),
    .out25(decoder_1_out25), .out26(decoder_1_out26), .out27(decoder_1_out27), .out28(decoder_1_out28),
    .out29(decoder_1_out29), .out30(decoder_1_out30), .out31(decoder_1_out31), .sel(Register_File_Select),
    .en(or_1_out));  // open: out0
  Register #(.width(32)) x0 (.en(1'b0), .clk(Register_File_Clk), .Q(x0_q), .clr(Reset));  // open: D
  Register #(.width(32)) x8 (.en(decoder_1_out8), .clk(Register_File_Clk), .clr(Reset));  // open: D, Q
  Register #(.width(32)) x16 (.en(decoder_1_out16), .clk(Register_File_Clk), .clr(Reset));  // open: D, Q
  Register #(.width(32)) x24 (.en(decoder_1_out24), .clk(Register_File_Clk), .clr(Reset));  // open: D, Q
  Register #(.width(32)) x1 (.en(decoder_1_out1), .clk(Register_File_Clk), .clr(Reset));  // open: D, Q
  Register #(.width(32)) x9 (.en(decoder_1_out9), .clk(Register_File_Clk), .clr(Reset));  // open: D, Q
  Register #(.width(32)) x17 (.en(decoder_1_out17), .clk(Register_File_Clk), .clr(Reset));  // open: D, Q
  Register #(.width(32)) x25 (.en(decoder_1_out25), .clk(Register_File_Clk), .clr(Reset));  // open: D, Q
  Register #(.width(32)) x2 (.en(decoder_1_out2), .clk(Register_File_Clk), .clr(Reset));  // open: D, Q
  Register #(.width(32)) x10 (.en(decoder_1_out10), .clk(Register_File_Clk), .clr(Reset));  // open: D, Q
  Register #(.width(32)) x18 (.en(decoder_1_out18), .clk(Register_File_Clk), .clr(Reset));  // open: D, Q
  Register #(.width(32)) x26 (.en(decoder_1_out26), .clk(Register_File_Clk), .clr(Reset));  // open: D, Q
  Register #(.width(32)) x3 (.en(decoder_1_out3), .clk(Register_File_Clk), .clr(Reset));  // open: D, Q
  Register #(.width(32)) x11 (.en(decoder_1_out11), .clk(Register_File_Clk), .clr(Reset));  // open: D, Q
  Register #(.width(32)) x19 (.en(decoder_1_out19), .clk(Register_File_Clk), .clr(Reset));  // open: D, Q
  Register #(.width(32)) x27 (.en(decoder_1_out27), .clk(Register_File_Clk), .clr(Reset));  // open: D, Q
  Register #(.width(32)) x4 (.en(decoder_1_out4), .clk(Register_File_Clk), .clr(Reset));  // open: D, Q
  Register #(.width(32)) x12 (.en(decoder_1_out12), .clk(Register_File_Clk), .clr(Reset));  // open: D, Q
  Register #(.width(32)) x20 (.en(decoder_1_out20), .clk(Register_File_Clk), .clr(Reset));  // open: D, Q
  Register #(.width(32)) x28 (.en(decoder_1_out28), .clk(Register_File_Clk), .clr(Reset));  // open: D, Q
  Register #(.width(32)) x5 (.en(decoder_1_out5), .clk(Register_File_Clk), .clr(Reset));  // open: D, Q
  Register #(.width(32)) x13 (.en(decoder_1_out13), .clk(Register_File_Clk), .clr(Reset));  // open: D, Q
  Register #(.width(32)) x21 (.en(decoder_1_out21), .clk(Register_File_Clk), .clr(Reset));  // open: D, Q
  Register #(.width(32)) x29 (.en(decoder_1_out29), .clk(Register_File_Clk), .clr(Reset));  // open: D, Q
  Register #(.width(32)) x6 (.en(decoder_1_out6), .clk(Register_File_Clk), .clr(Reset));  // open: D, Q
  Register #(.width(32)) x14 (.en(decoder_1_out14), .clk(Register_File_Clk), .clr(Reset));  // open: D, Q
  Register #(.width(32)) x22 (.en(decoder_1_out22), .clk(Register_File_Clk), .clr(Reset));  // open: D, Q
  Register #(.width(32)) x30 (.en(decoder_1_out30), .clk(Register_File_Clk), .clr(Reset));  // open: D, Q
  Register #(.width(32)) x7 (.en(decoder_1_out7), .clk(Register_File_Clk), .clr(Reset));  // open: D, Q
  Register #(.width(32)) x15 (.en(decoder_1_out15), .clk(Register_File_Clk), .clr(Reset));  // open: D, Q
  Register #(.width(32)) x23 (.en(decoder_1_out23), .clk(Register_File_Clk), .clr(Reset));  // open: D, Q
  Register #(.width(32)) x31 (.en(decoder_1_out31), .clk(Register_File_Clk), .clr(Reset));  // open: D, Q
  Multiplexer #(.select(5), .width(32)) multiplexer_1 (.sel(undriven));  // open: in0, in1, in2, in3, in4, in5, in6, in7, in8, in9, in10, in11, in12, in13, in14, in15, in16, in17, in18, in19, in20, in21, in22, in23, in24, in25, in26, in27, in28, in29, in30, in31, out
endmodule
